# Fritzing sketch handlebars (saved by Fritzing 0.9.3b)
stripboards: 1

parts:
  Part1 = Arduino Nano (Rev3.0)
  Part2 = Bluetooth HC-05 Macho
  R1 = Resistor [tolerance=±5% resistance=220 package="2512 [SMD]"]
  R2 = Resistor [tolerance=±5% resistance=220 package="2512 [SMD]"]
  BAT1 = 18650 battery holder [package=battery-18650-kit]
  S2 = Taiway 100-SP-X-T1 SPDT Miniature Toggle Switch [part_number=100-SP-X-T1-0-0-B1-M2 package=THT]
  S1 = Taiway 100-SP-X-T1 SPDT Miniature Toggle Switch [part_number=100-SP-X-T1-0-0-B1-M2 package=THT]
  Part3 = TP4056 Charger

nets:
  N1: Part1.D1/TX, Part2.RXD
  N2: Part1.D0/RX, Part2.TXD
  GND: Part1.GND, Part2.GND, R1.Pin_1, R2.Pin_0, S2.L2, Part3.IN-, Part3.BAT-
  5V: Part1.5V, Part2.VCC, BAT1.+, S1.COM, Part3.IN+, Part3.BAT+
  N3: Part1.A1, R1.Pin_0
  N4: Part1.A0, R2.Pin_1
  N5: BAT1.-, S2.COM

custom parts:
  18650 battery holder: 18650 Battery Holder
