# Fritzing sketch lights (saved by Fritzing 0.9.3b)
breadboards: 2

parts:
  U1 = atmega328 [package=dip]
  Part1 = Bluetooth HC-05 Macho
  8x8_LED_Modul_mit_MAX1 = 8x8 LED Modul mit MAX7219 [package=THT]
  8x8_LED_Modul_mit_MAX2 = 8x8 LED Modul mit MAX7219 [package=THT]
  BAT1 = 18650 battery holder [package=battery-18650-kit]
  Part2 = TP4056 Charger
  S1 = Taiway 100-SP-X-T1 SPDT Miniature Toggle Switch [part_number=100-SP-X-T1-0-0-B1-M1 package=THT]

nets:
  N1: U1.D0_(RX), Part1.TXD
  N2: U1.D1_(TX), Part1.RXD
  VCC: U1.VCC, Part1.VCC, 8x8_LED_Modul_mit_MAX2.VCC_Eingang
  N3: U1.GND#7, Part1.GND, 8x8_LED_Modul_mit_MAX2.GND_Eingang
  N4: U1.D9_(PWM), 8x8_LED_Modul_mit_MAX2.CLK_Eingang
  N5: U1.D11_(PWM), 8x8_LED_Modul_mit_MAX2.CS_Eingang
  N6: U1.D13, 8x8_LED_Modul_mit_MAX2.DIN_Eingang
  N7: U1.AVCC, BAT1.+, Part2.IN+, Part2.BAT+
  N8: U1.GND#21, S1.L1
  N9: 8x8_LED_Modul_mit_MAX1.VCC_Eingang, 8x8_LED_Modul_mit_MAX2.VCC_Ausgang
  N10: 8x8_LED_Modul_mit_MAX1.GND_Eingang, 8x8_LED_Modul_mit_MAX2.GND_Ausgang
  N11: 8x8_LED_Modul_mit_MAX1.DIN_Eingang, 8x8_LED_Modul_mit_MAX2.DOUT_Ausgang
  N12: 8x8_LED_Modul_mit_MAX1.CS_Eingang, 8x8_LED_Modul_mit_MAX2.CS_Ausgang
  N13: 8x8_LED_Modul_mit_MAX1.CLK_Eingang, 8x8_LED_Modul_mit_MAX2.CLK_Ausgang
  N14: BAT1.-, Part2.IN-, Part2.BAT-, S1.COM

custom parts:
  18650 battery holder: 18650 Battery Holder
